// Digital circuit 2x74590_16bit_cnt_bus.dig as structural Verilog
module _2x74590_16bit_cnt_bus (
  input  nCLR,
  input  CLK,
  output [15:0] Q,
  output nRCO
);

  wire and_1_out, not_1_out;

  and and_1 (and_1_out, not_1_out, nCLR);
  _74590 _74590_1 (
    .pin1(Q[9]), .pin2(Q[10]), .pin3(Q[11]), .pin4(Q[12]), .pin5(Q[13]), .pin6(Q[14]), .pin7(Q[15]),
    .pin8(1'b0), .pin9(nRCO), .pin10(nCLR), .pin11(and_1_out), .pin12(1'b0), .pin13(and_1_out), .pin14(1'b0),
    .pin15(Q[8]), .pin16(1'b1));
  _74590 _74590_2 (
    .pin1(Q[1]), .pin2(Q[2]), .pin3(Q[3]), .pin4(Q[4]), .pin5(Q[5]), .pin6(Q[6]), .pin7(Q[7]), .pin8(1'b0),
    .pin10(nCLR), .pin11(CLK), .pin12(1'b0), .pin13(CLK), .pin14(1'b0), .pin15(Q[0]), .pin16(1'b1));  // open: pin9
  not not_1 (not_1_out, Q[7]);

  // Notes on the sheet:
  //   CLK: Hz: 10000
endmodule
