// Digital circuit 2x74688_16bit_comp_bus.dig as structural Verilog
module _2x74688_16bit_comp_bus (
  input  [15:0] P,
  input  [15:0] Q,
  output EQ,
  output nEQ
);

  wire _74688_comp_bus_1_neq, _74688_comp_bus_2_neq, not_1_out, not_2_out;

  _74688_comp_bus _74688_comp_bus_1 (.nOE(1'b0), .P(P[7:0]), .Q(Q[7:0]), .nEQ(_74688_comp_bus_1_neq));
  _74688_comp_bus _74688_comp_bus_2 (.nOE(1'b0), .P(P[15:8]), .Q(Q[15:8]), .nEQ(_74688_comp_bus_2_neq));
  not not_1 (not_1_out, _74688_comp_bus_1_neq);
  not not_2 (not_2_out, _74688_comp_bus_2_neq);
  and and_1 (EQ, not_1_out, not_2_out);
  not not_3 (nEQ, EQ);
endmodule
