// Digital circuit 74590_counter_bus.dig as structural Verilog
module _74590_counter_bus (
  input  nCCLR,
  input  CLK,
  output nRCO,
  output [7:0] Q
);

  _74590 _74590_1 (
    .pin1(Q[1]), .pin2(Q[2]), .pin3(Q[3]), .pin4(Q[4]), .pin5(Q[5]), .pin6(Q[6]), .pin7(Q[7]), .pin8(1'b0),
    .pin9(nRCO), .pin10(nCCLR), .pin11(CLK), .pin12(1'b0), .pin13(CLK), .pin14(1'b0), .pin15(Q[0]),
    .pin16(1'b1));
endmodule
