// Digital circuit 74688_comp_bus.dig as structural Verilog
module _74688_comp_bus (
  input  nOE,
  input  [7:0] P,
  input  [7:0] Q,
  output nEQ
);

  _74688 _74688_1 (
    .pin1(nOE), .pin2(P[0]), .pin3(Q[0]), .pin4(P[1]), .pin5(Q[1]), .pin6(P[2]), .pin7(Q[2]), .pin8(P[3]),
    .pin9(Q[3]), .pin10(1'b0), .pin11(P[4]), .pin12(Q[4]), .pin13(P[5]), .pin14(Q[5]), .pin15(P[6]),
    .pin16(Q[6]), .pin17(P[7]), .pin18(Q[7]), .pin19(nEQ), .pin20(1'b1));
endmodule
