// Digital circuit double_16bit_clk.dig as structural Verilog
module double_16bit_clk (
  input  CLK_RAW,
  input  [15:0] D_CLK1,
  input  [15:0] D_CLK2,
  output CLK_OUT
);

  wire _2x74590_16bit_cnt_bus_1_nrco, _2x74590_16bit_cnt_bus_2_nrco, _2x74688_16bit_comp_bus_1_neq,
       _2x74688_16bit_comp_bus_2_neq, CLK_d14;
  wire [15:0] _2x74590_16bit_cnt_bus_1_q, _2x74590_16bit_cnt_bus_2_q;

  _2x74590_16bit_cnt_bus _2x74590_16bit_cnt_bus_1 (
    .nCLR(_2x74688_16bit_comp_bus_1_neq), .CLK(CLK_RAW), .Q(_2x74590_16bit_cnt_bus_1_q),
    .nRCO(_2x74590_16bit_cnt_bus_1_nrco));
  _2x74590_16bit_cnt_bus _2x74590_16bit_cnt_bus_2 (
    .nCLR(_2x74688_16bit_comp_bus_2_neq), .CLK(CLK_d14), .Q(_2x74590_16bit_cnt_bus_2_q),
    .nRCO(_2x74590_16bit_cnt_bus_2_nrco));
  _2x74688_16bit_comp_bus _2x74688_16bit_comp_bus_1 (
    .P(_2x74590_16bit_cnt_bus_1_q), .Q(D_CLK1), .EQ(CLK_d14), .nEQ(_2x74688_16bit_comp_bus_1_neq));
  _2x74688_16bit_comp_bus _2x74688_16bit_comp_bus_2 (
    .P(_2x74590_16bit_cnt_bus_2_q), .Q(D_CLK2), .EQ(CLK_OUT), .nEQ(_2x74688_16bit_comp_bus_2_neq));

  // Other names for the same wires on the sheet: CLK = CLK_RAW; CLK_d28 = CLK_OUT

  // Notes on the sheet:
  //   CLK_RAW: Hz: 2147483647
endmodule
