// Digital circuit sim.dig as structural Verilog
module sim (
  input  VCC,
  input  GND,
  input  CLK_RAW
);

  wire _74595_1_pin9, _74595_2_pin9, _74595_3_pin9, _74595_4_pin9, _74688_comp_bus_1_neq, CLK_d28,
       DIV_SELECT_out, nor_1_out, not_1_out, or_1_out;
  wire [7:0] _74590_counter_bus_1_q, _74595_1_pin7;
  wire [15:0] multiplexer_1_out, multiplexer_2_out;
  wire [31:8] _74595_2_pin7;

  Multiplexer #(.Bits(16)) multiplexer_1 (
    .sel(DIV_SELECT_out), .in_0(16'h4000), .in_1(16'h80), .out(multiplexer_1_out));
  Multiplexer #(.Bits(16)) multiplexer_2 (.sel(DIV_SELECT_out), .in_0(16'h4000), .in_1(16'h1), .out(multiplexer_2_out));
  DipSwitch #(.dipDefault("true")) DIV_SELECT (.out(DIV_SELECT_out));
  PowerSupply powersupply_1 (.VDD(VCC), .GND(GND));
  double_16bit_clk double_16bit_clk_1 (
    .CLK_RAW(CLK_RAW), .D_CLK1(multiplexer_2_out), .D_CLK2(multiplexer_1_out), .CLK_OUT(CLK_d28));
  _74688_comp_bus _74688_comp_bus_1 (.nOE(1'b0), .P(8'hdd), .Q(_74590_counter_bus_1_q), .nEQ(_74688_comp_bus_1_neq));
  _74590_counter_bus _74590_counter_bus_1 (
    .nCCLR(_74688_comp_bus_1_neq), .CLK(CLK_d28), .Q(_74590_counter_bus_1_q));  // open: nRCO
  not not_1 (not_1_out, _74688_comp_bus_1_neq);
  or or_1 (or_1_out, _74595_4_pin9, nor_1_out);
  _74595 _74595_1 (
    .pin1(_74595_1_pin7[1]), .pin2(_74595_1_pin7[2]), .pin3(_74595_1_pin7[3]), .pin4(_74595_1_pin7[4]),
    .pin5(_74595_1_pin7[5]), .pin6(_74595_1_pin7[6]), .pin7(_74595_1_pin7[7]), .pin8(1'b0),
    .pin9(_74595_1_pin9), .pin10(1'b1), .pin11(not_1_out), .pin12(CLK_d28), .pin13(1'b0), .pin14(or_1_out),
    .pin15(_74595_1_pin7[0]), .pin16(1'b1));
  LED led_1 (.in(_74595_1_pin7[0]));
  LED led_2 (.in(_74595_1_pin7[1]));
  LED led_3 (.in(_74595_1_pin7[2]));
  LED led_4 (.in(_74595_1_pin7[3]));
  LED led_5 (.in(_74595_1_pin7[4]));
  LED led_6 (.in(_74595_1_pin7[5]));
  LED led_7 (.in(_74595_1_pin7[6]));
  _74595 _74595_2 (
    .pin1(_74595_2_pin7[9]), .pin2(_74595_2_pin7[10]), .pin3(_74595_2_pin7[11]), .pin4(_74595_2_pin7[12]),
    .pin5(_74595_2_pin7[13]), .pin6(_74595_2_pin7[14]), .pin7(_74595_2_pin7[15]), .pin8(1'b0),
    .pin9(_74595_2_pin9), .pin10(1'b1), .pin11(not_1_out), .pin12(CLK_d28), .pin13(1'b0),
    .pin14(_74595_1_pin9), .pin15(_74595_2_pin7[8]), .pin16(1'b1));
  LED led_8 (.in(_74595_1_pin7[7]));
  LED led_9 (.in(_74595_2_pin7[8]));
  LED led_10 (.in(_74595_2_pin7[9]));
  LED led_11 (.in(_74595_2_pin7[10]));
  nor nor_1 (nor_1_out, _74595_1_pin7[0], _74595_1_pin7[1], _74595_1_pin7[2], _74595_1_pin7[3], _74595_1_pin7[4], _74595_1_pin7[5], _74595_1_pin7[6], _74595_1_pin7[7], _74595_2_pin7[8], _74595_2_pin7[9], _74595_2_pin7[10], _74595_2_pin7[11], _74595_2_pin7[12], _74595_2_pin7[13], _74595_2_pin7[14], _74595_2_pin7[15], _74595_2_pin7[16], _74595_2_pin7[17], _74595_2_pin7[18], _74595_2_pin7[19], _74595_2_pin7[20], _74595_2_pin7[21], _74595_2_pin7[22], _74595_2_pin7[23], _74595_2_pin7[24], _74595_2_pin7[25], _74595_2_pin7[26], _74595_2_pin7[27], _74595_2_pin7[28], _74595_2_pin7[29], _74595_2_pin7[30], _74595_2_pin7[31]);
  LED led_12 (.in(_74595_2_pin7[11]));
  LED led_13 (.in(_74595_2_pin7[12]));
  LED led_14 (.in(_74595_2_pin7[13]));
  LED led_15 (.in(_74595_2_pin7[14]));
  LED led_16 (.in(_74595_2_pin7[15]));
  LED led_17 (.in(_74595_2_pin7[16]));
  LED led_18 (.in(_74595_2_pin7[17]));
  LED led_19 (.in(_74595_2_pin7[18]));
  LED led_20 (.in(_74595_2_pin7[19]));
  LED led_21 (.in(_74595_2_pin7[20]));
  LED led_22 (.in(_74595_2_pin7[21]));
  LED led_23 (.in(_74595_2_pin7[22]));
  LED led_24 (.in(_74595_2_pin7[23]));
  LED led_25 (.in(_74595_2_pin7[24]));
  LED led_26 (.in(_74595_2_pin7[25]));
  LED led_27 (.in(_74595_2_pin7[26]));
  _74595 _74595_3 (
    .pin1(_74595_2_pin7[17]), .pin2(_74595_2_pin7[18]), .pin3(_74595_2_pin7[19]), .pin4(_74595_2_pin7[20]),
    .pin5(_74595_2_pin7[21]), .pin6(_74595_2_pin7[22]), .pin7(_74595_2_pin7[23]), .pin8(1'b0),
    .pin9(_74595_3_pin9), .pin10(1'b1), .pin11(not_1_out), .pin12(CLK_d28), .pin13(1'b0),
    .pin14(_74595_2_pin9), .pin15(_74595_2_pin7[16]), .pin16(1'b1));
  LED led_28 (.in(_74595_2_pin7[27]));
  LED led_29 (.in(_74595_2_pin7[28]));
  LED led_30 (.in(_74595_2_pin7[29]));
  LED led_31 (.in(_74595_2_pin7[30]));
  LED led_32 (.in(_74595_2_pin7[31]));
  _74595 _74595_4 (
    .pin1(_74595_2_pin7[25]), .pin2(_74595_2_pin7[26]), .pin3(_74595_2_pin7[27]), .pin4(_74595_2_pin7[28]),
    .pin5(_74595_2_pin7[29]), .pin6(_74595_2_pin7[30]), .pin7(_74595_2_pin7[31]), .pin8(1'b0),
    .pin9(_74595_4_pin9), .pin10(1'b1), .pin11(not_1_out), .pin12(CLK_d28), .pin13(1'b0),
    .pin14(_74595_3_pin9), .pin15(_74595_2_pin7[24]), .pin16(1'b1));

  // Other names for the same wires on the sheet: CLK = CLK_RAW

  // Notes on the sheet:
  //   VCC: default 1
  //   CLK_RAW: Hz: 2147483647
endmodule
